# Fritzing sketch complete_schema_esp32_feather (saved by Fritzing 0.9.6b)
breadboards: 2

parts:
  S2 = SWITCH-MOMENTARY-2 [package=tactile-pth-12mm]
  S3 = SWITCH-MOMENTARY-2 [package=tactile-pth-12mm]
  S4 = SWITCH-MOMENTARY-2 [package=tactile-pth-12mm]
  S5 = SWITCH-MOMENTARY-2 [package=tactile-pth-12mm]
  Grove1 = Grove OLED 128x96
  U1 = PCF8574 [package="DIP16 [THT]"]
  Matrix_keypad1 = KEYPAD 4x4
  switch1 = Rotary_Switch_12x1
  Part1 = Adafruit HUZZAH32 ESP32 Feather [part_number="Adafruit #3405"]

nets:
  GND: S2.1, S3.1, S4.1, S5.1, Grove1.GND, U1.GND, switch1.0, Part1.GND
  N1: S2.2, Part1.IO15_A8
  N2: S3.2, Part1.IO33_A9
  N3: S4.2, Part1.IO14_A6
  N4: S5.2, Part1.IO32_A7
  N5: Grove1.SDA, U1.SDA, Part1.SDA
  N6: Grove1.SCL, U1.SCL, Part1.SCL
  N7: U1.P0, Matrix_keypad1.row1
  N8: U1.P1, Matrix_keypad1.row2
  N9: U1.P2, Matrix_keypad1.row3
  N10: U1.P3, Matrix_keypad1.row4
  N11: U1.P4, Matrix_keypad1.col1
  N12: U1.P5, Matrix_keypad1.col2
  N13: U1.P6, Matrix_keypad1.col3
  N14: U1.P7, Matrix_keypad1.col4
  VCC: U1.VCC, Part1.3.3V
  N15: switch1.6, Part1.SCK
  N16: switch1.7, Part1.MOSI
  N17: switch1.8, Part1.MISO
  N18: switch1.9, Part1.IO16

custom parts:
  KEYPAD 4x4: Matrix keypad 16 buttons, 4 rows x 4 columns
